# Fritzing sketch Project_Fritzing_Diagram (saved by Fritzing 0.9.3b)
breadboards: 3

parts:
  Part1 = PocketBeagle
  U1 = POT [package=alps_pot]
  Part3 = 0.56" 7-segment LED Backpack [part_number=878]
  BAT1 = Battery Holders [package=lipo-1100mAh]
  R3 = Resistor [tolerance=±5% resistance=220 package="2010 [SMD]"]
  R4 = Resistor [tolerance=±5% resistance=220 package="2010 [SMD]"]
  Heating_Pad = Resistor [tolerance=±5% resistance=220 package=THT]
  Q2 = TIP120 Hi-Current Darlington Transistor
  DS1 = DS18B20 1-Wire Temperature Sensor [part_number=DS18B20]
  R5 = Resistor [tolerance=±5% resistance=220 package="0402 [SMD]"]
  D1 = Diode [package=diode-1n4148]
  LED1 = LED - 5mm [color="Red (633nm)" package="5 mm [THT]"]
  LED2 = LED - 5mm [color="Red (633nm)" package="5 mm [THT]"]
  LED3 = LED - 5mm [color="Red (633nm)" package="5 mm [THT]"]

nets (from the schematic view):
  GND: Part1.GND, U1.A, Part3.GND, BAT1.-, Heating_Pad.Pin_1, DS1.GND, LED1.cathode, LED2.cathode, LED3.cathode
  N1: Part1.VOUT, DS1.VDD, R5.Pin_1
  N2: Part1.I2C1.SCL, R3.Pin_0
  N3: Part1.I2C1.SDA, R4.Pin_0
  N4: Part1.GPIO47, LED1.anode
  N5: Part1.GPIO64, LED2.anode
  N6: Part1.GPIO46, LED3.anode
  3.3V: Part1.3.3V, U1.E, Part3.VDD
  N7: Part1.GPIO48, D1.A
  N8: Part1.AIN5/GPIO86, U1.S
  N9: Part3.SCL, R3.Pin_1
  N10: Part3.SDA, R4.Pin_1
  N11: BAT1.+, Q2.COLLECTOR
  N12: Heating_Pad.Pin_0, Q2.EMITTER
  N13: Q2.BASE, D1.C
  N14: DS1.DQ, R5.Pin_0

custom parts:
  0.56" 7-segment LED Backpack: This 0.56" 7-segment LED display includes a driver chip for simple control via an I2C interface. The backpack features address-selection jumpers so you can connect up to eight displays on a single I2C bus.
